# Fritzing sketch b-car_pcb_layout_rev1 (saved by Fritzing 0.9.3b)
circuit board: 8.1cm x 5cm
breadboards: 1

parts:
  74HC04-1 = 74HC04_HEX_INVERTER [package=dil14]
  74HC04-2 = 74HC04_HEX_INVERTER [package=dil14]
  4116R-R2R-1 = DIP - 16 pins [chip_label=4116R-R2R package="DIP (Dual Inline) [THT]"]
  R1 = Resistor [tolerance=±5% resistance=47k package=THT]
  R1_2 = Resistor [tolerance=±5% resistance=47k package=THT]
  R1_3 = Resistor [tolerance=±5% resistance=47k package=THT]
  R1_4 = Resistor [tolerance=±5% resistance=47k package=THT]
  R1_5 = Resistor [tolerance=±5% resistance=47k package=THT]
  4116R-R2R-2 = DIP - 16 pins [chip_label=4116R-R2R package="DIP (Dual Inline) [THT]"]
  R1_6 = Resistor [tolerance=±5% resistance=47k package=THT]
  R1_7 = Resistor [tolerance=±5% resistance=47k package=THT]
  R1_8 = Resistor [tolerance=±5% resistance=47k package=THT]
  R1_9 = Resistor [tolerance=±5% resistance=47k package=THT]
  R1_10 = Resistor [tolerance=±5% resistance=47k package=THT]
  ATTiny85 = attiny85 [package=dip]
  X1 = USB Connectors [package=usb-mb-h]
  R2 = Resistor [tolerance=±5% resistance=68 package=THT]
  R3 = Resistor [tolerance=±5% resistance=1.5k package=THT]
  R2_2 = Resistor [tolerance=±5% resistance=68 package=THT]

nets:
  N1: 74HC04-1.1A, R1_6.Pin_1
  N2: 74HC04-1.1Y, 4116R-R2R-2.pin8
  N3: 74HC04-1.2A, R1_8.Pin_1
  N4: 74HC04-1.2Y, 4116R-R2R-2.pin7
  N5: 74HC04-1.3A, R1_7.Pin_1
  N6: 74HC04-1.3Y, 4116R-R2R-2.pin6
  GND: 74HC04-1.GND, 74HC04-2.GND, 4116R-R2R-1.pin9, 4116R-R2R-2.pin9, ATTiny85.Pin_4, X1.GND
  N7: 74HC04-1.4Y, 4116R-R2R-1.pin6
  N8: 74HC04-1.4A, R1_3.Pin_0
  N9: 74HC04-1.5Y, 4116R-R2R-1.pin5
  N10: 74HC04-1.5A, R1_2.Pin_0
  N11: 74HC04-1.6Y, 4116R-R2R-1.pin4
  N12: 74HC04-1.6A, R1.Pin_0
  5V: 74HC04-1.VCC, 74HC04-2.VCC, R1.Pin_1, R1_2.Pin_1, R1_3.Pin_1, R1_4.Pin_1, R1_5.Pin_1, R1_6.Pin_0, R1_7.Pin_0, R1_8.Pin_0, R1_9.Pin_0, R1_10.Pin_0, ATTiny85.Pin_8, R3.Pin_1
  N13: 74HC04-2.1A, R1_9.Pin_1
  N14: 74HC04-2.1Y, 4116R-R2R-2.pin5
  N15: 74HC04-2.2A, R1_10.Pin_1
  N16: 74HC04-2.2Y, 4116R-R2R-2.pin4
  N17: 74HC04-2.5Y, 4116R-R2R-1.pin8
  N18: 74HC04-2.5A, R1_5.Pin_0
  N19: 74HC04-2.6Y, 4116R-R2R-1.pin7
  N20: 74HC04-2.6A, R1_4.Pin_0
  N21: 4116R-R2R-1.pin13, ATTiny85.Pin_7
  N22: 4116R-R2R-2.pin13, ATTiny85.Pin_3, R2_2.Pin_0
  N23: ATTiny85.Pin_2, R2.Pin_0
  N24: X1.D+, R2_2.Pin_1
  N25: X1.D-, R2.Pin_1, R3.Pin_0

notes:
  PB4
  PB3
  PB5
  GND
  5V
  PB2
  PB0
  S1
  S2
  S3
  S4
  S5
  S10
  S9
  S8
  S7
  S6
  Power
  3A
  3Y
  4A
  4Y
  b-car rev. 1
  https://github.com/copyrights/b-car

custom parts:
  DIP - 16 pins: A DIP stand-in part for whatever IC you want. With 16 pins on a 300mil dual inline package (DIP) footprint.
